// Logisim project caesercipher01.circ as structural Verilog: 7 circuits, main circuit IS_UPPERCASE
module IS_UPPERCASE (
  input  [7:0] char,
  output is_upper
);

  wire not_1_out, not_2_out, subtractor_1_bout, subtractor_2_bout;

  Subtractor subtractor_1 (.a(char), .b(8'h41), .bout(subtractor_1_bout));  // open: out, bin
  Subtractor subtractor_2 (.a(8'h5a), .b(char), .bout(subtractor_2_bout));  // open: out, bin
  not not_1 (not_1_out, subtractor_1_bout);
  not not_2 (not_2_out, subtractor_2_bout);
  and and_1 (is_upper, not_1_out, not_2_out);
endmodule

module IS_LOWERCASE (
  input  [7:0] char,
  output is_lower
);

  wire not_1_out, not_2_out, subtractor_1_bout, subtractor_2_bout;

  Subtractor subtractor_1 (.a(char), .b(8'h61), .bout(subtractor_1_bout));  // open: out, bin
  Subtractor subtractor_2 (.a(8'h7a), .b(char), .bout(subtractor_2_bout));  // open: out, bin
  not not_1 (not_1_out, subtractor_1_bout);
  not not_2 (not_2_out, subtractor_2_bout);
  and and_1 (is_lower, not_1_out, not_2_out);
endmodule

module BASE_SELECTOR (
  input  is_lower,
  input  is_upper,
  output [7:0] base
);

  Multiplexer #(.select(2), .width(8)) multiplexer_1 (
    .in0({8{1'b0}}), .in1(8'h61), .in2(8'h41), .in3(8'h41), .out(base), .sel({is_upper, is_lower}));
endmodule

module ccencoder (
  input  [7:0] char_in,
  input  [7:0] shift,
  output [7:0] encoded_char
);

  wire is_lowercase_1_is_lower, is_uppercase_1_is_upper, or_1_out;
  wire [7:0] adder_1_out, adder_2_out, base_selector_1_base, mod_26_1_mod_out, subtractor_1_out;

  IS_LOWERCASE is_lowercase_1 (.char(char_in), .is_lower(is_lowercase_1_is_lower));
  IS_UPPERCASE is_uppercase_1 (.char(char_in), .is_upper(is_uppercase_1_is_upper));
  or or_1 (or_1_out, is_lowercase_1_is_lower, is_uppercase_1_is_upper);
  BASE_SELECTOR base_selector_1 (
    .is_lower(is_lowercase_1_is_lower), .is_upper(is_uppercase_1_is_upper), .base(base_selector_1_base));
  Subtractor subtractor_1 (.a(char_in), .b(base_selector_1_base), .out(subtractor_1_out));  // open: bin, bout
  Adder adder_1 (.a(subtractor_1_out), .b(shift), .out(adder_1_out));  // open: cin, cout
  mod_26 mod_26_1 (.value_in(adder_1_out), .mod_out(mod_26_1_mod_out));
  Adder adder_2 (.a(mod_26_1_mod_out), .b(base_selector_1_base), .out(adder_2_out));  // open: cin, cout
  Multiplexer #(.width(8)) multiplexer_1 (.in0(char_in), .in1(adder_2_out), .out(encoded_char), .sel(or_1_out));

  // Notes on the sheet:
  //   valid_char
endmodule

module mod_26 (
  input  [7:0] value_in,
  output [7:0] mod_out
);

  wire comparator_1_eq, comparator_1_gt, or_1_out;
  wire [7:0] subtractor_1_out;

  Comparator comparator_1 (.a(value_in), .b(8'h1a), .gt(comparator_1_gt), .eq(comparator_1_eq));  // open: lt
  Subtractor subtractor_1 (.a(value_in), .b(8'h1a), .out(subtractor_1_out));  // open: bin, bout
  or or_1 (or_1_out, comparator_1_gt, comparator_1_eq);
  Multiplexer #(.width(8)) multiplexer_1 (.in0(value_in), .in1(subtractor_1_out), .out(mod_out), .sel(or_1_out));
endmodule

module ccdecoder (
  input  [7:0] char_in,
  input  [7:0] shift,
  output [7:0] decoded_char
);

  wire is_lowercase_1_is_lower, is_uppercase_1_is_upper, or_1_out;
  wire [7:0] adder_1_out, adder_2_out, base_selector_1_base, mod_26_1_mod_out, subtractor_1_out,
       subtractor_2_out;

  Subtractor subtractor_1 (.a(8'h1a), .b(shift), .out(subtractor_1_out));  // open: bin, bout
  IS_LOWERCASE is_lowercase_1 (.char(char_in), .is_lower(is_lowercase_1_is_lower));
  IS_UPPERCASE is_uppercase_1 (.char(char_in), .is_upper(is_uppercase_1_is_upper));
  or or_1 (or_1_out, is_lowercase_1_is_lower, is_uppercase_1_is_upper);
  BASE_SELECTOR base_selector_1 (
    .is_lower(is_lowercase_1_is_lower), .is_upper(is_uppercase_1_is_upper), .base(base_selector_1_base));
  Subtractor subtractor_2 (.a(char_in), .b(base_selector_1_base), .out(subtractor_2_out));  // open: bin, bout
  Adder adder_1 (.a(subtractor_2_out), .b(subtractor_1_out), .out(adder_1_out));  // open: cin, cout
  mod_26 mod_26_1 (.value_in(adder_1_out), .mod_out(mod_26_1_mod_out));
  Adder adder_2 (.a(mod_26_1_mod_out), .b(base_selector_1_base), .out(adder_2_out));  // open: cin, cout
  Multiplexer #(.width(8)) multiplexer_1 (.in0(char_in), .in1(adder_2_out), .out(decoded_char), .sel(or_1_out));
endmodule

module Caesar_Testbench (
  input  [7:0] char_in,
  input  [4:0] Shift,
  input  in_3,
  output [7:0] final_output
);

  wire [7:0] bit_extender_1_out, ccdecoder_1_decoded_char, ccencoder_1_encoded_char;

  assign bit_extender_1_out = {{3{1'b0}}, Shift};  // Bit_Extender bit_extender_1
  // Probe on ccencoder_1_encoded_char
  ccencoder ccencoder_1 (.char_in(char_in), .shift(bit_extender_1_out), .encoded_char(ccencoder_1_encoded_char));
  // Probe on ccdecoder_1_decoded_char
  ccdecoder ccdecoder_1 (.char_in(char_in), .shift(bit_extender_1_out), .decoded_char(ccdecoder_1_decoded_char));
  Multiplexer #(.width(8)) multiplexer_1 (
    .in0(ccencoder_1_encoded_char), .in1(ccdecoder_1_decoded_char), .out(final_output), .sel(in_3));
endmodule
